# Fritzing sketch proj (saved by Fritzing 0.9.3b)
circuit board: 8.46667cm x 5.64444cm

parts:
  U1 = ESP8266 WiFi Module [part_number=ESP8266]
  Arduino_Nano = Arduino Nano (Rev3.0)
  R1 = Resistor [tolerance=±5% resistance=1k package="0402 [SMD]"]
  R2 = Resistor [tolerance=±5% resistance=2k package="0402 [SMD]"]
  R3 = Resistor [tolerance=±5% resistance=10k package="0805 [SMD]"]
  LED1 = LED - 3mm [color="Red (633nm)" package="3 mm [THT]"]
  Pulse_Sensor = Pulse Sensor [package=SIP]
  S1 = Pushbutton [package="[THT]"]

nets:
  N1: U1.RXD, R1.Pin_1, R2.Pin_0
  VCC: U1.VCC, Arduino_Nano.3V3, R3.Pin_1, Pulse_Sensor.Vcc, S1.Pin_1, S1.Pin_2
  N2: U1.CH_PD, R3.Pin_0
  GND: U1.GND, Arduino_Nano.GND, R2.Pin_1, LED1.cathode, Pulse_Sensor.GND
  N3: U1.TXD, Arduino_Nano.D3
  N4: Arduino_Nano.D2, R1.Pin_0
  N5: Arduino_Nano.D9, S1.Pin_3, S1.Pin_4
  N6: Arduino_Nano.D10, Pulse_Sensor.Signal
  N7: Arduino_Nano.D13/SCK, LED1.anode

custom parts:
  Pulse Sensor: Pulse Sensor Optical Heart Rate Monitor for Arduino and other microcontrollers
